# Fritzing sketch esp32c3-4axis (saved by Fritzing 0.9.10b)
circuit board: 8.98471cm x 8.51124cm
breadboards: 1

parts:
  J1 = female pin header, 16 pins [form="♀ (female)"]
  J2 = female pin header, 16 pins [form="♀ (female)"]
  X = Pololu A4988 [package=SO16]
  Y = Pololu A4988 [package=SO16]
  Z = Pololu A4988 [package=SO16]
  E = Pololu A4988 [package=SO16]
  X_en/step/dir/gnd = female pin header, 4 pins [form="♀ (female)"]
  Y_en/step/dir/gnd = female pin header, 4 pins [form="♀ (female)"]
  Z_en/step/dir/gnd = female pin header, 4 pins [form="♀ (female)"]
  E_en/step/dir/gnd = female pin header, 4 pins [form="♀ (female)"]
  X_motor = female pin header, 4 pins [form="♀ (female)"]
  Y_motor = female pin header, 4 pins [form="♀ (female)"]
  Z_motor = female pin header, 4 pins [form="♀ (female)"]
  E_motor = female pin header, 4 pins [form="♀ (female)"]
  X_endstop = female pin header, 3 pins [form="♀ (female)"]
  Y_endstop = female pin header, 3 pins [form="♀ (female)"]
  Z_endstop = female pin header, 3 pins [form="♀ (female)"]
  E_endstop = female pin header, 3 pins [form="♀ (female)"]
  J16 = Screw terminal - 2 pins [package=THT]
  Q1 = MOSFET-NCHANNEL [package=to220v]
  Q2 = MOSFET-NCHANNEL [package=to220v]
  U1 = Voltage Regulator - 5V [package="TO220 [THT]"]
  U2 = microSD Socket [package=usd-socket-pp]
  J19 = female pin header, 2 pins [form="♀ (female)"]  # not connected
  J20 = female pin header, 2 pins [form="♀ (female)"]  # not connected
  J21 = female pin header, 2 pins [form="♀ (female)"]  # not connected
  J22 = female pin header, 2 pins [form="♀ (female)"]  # not connected
  J24 = female pin header, 2 pins [form="♀ (female)"]  # not connected
  J25 = female pin header, 2 pins [form="♀ (female)"]  # not connected
  J27 = female pin header, 2 pins [form="♀ (female)"]  # not connected
  J28 = female pin header, 2 pins [form="♀ (female)"]  # not connected
  J30 = female pin header, 2 pins [form="♀ (female)"]  # not connected
  J31 = female pin header, 2 pins [form="♀ (female)"]  # not connected
  J32 = female pin header, 2 pins [form="♀ (female)"]  # not connected
  J33 = female pin header, 2 pins [form="♀ (female)"]  # not connected
  Hotend = Screw terminal - 2 pins [package=THT]  # not connected
  Bed = Screw terminal - 2 pins [package=THT]  # not connected
  Z2_motor = female pin header, 4 pins [form="♀ (female)"]
  Temp1 = female pin header, 2 pins [form="♀ (female)"]
  Temp2 = female pin header, 2 pins [form="♀ (female)"]
  Q3 = MOSFET-NCHANNEL [package=to220v]
  Fan = Screw terminal - 2 pins [package=THT]  # not connected
  R1 = Resistor [tolerance=±5% power=0.25 resistance=100k package=THT]  # not connected
  R2 = Resistor [tolerance=±5% power=0.25 resistance=100k package=THT]  # not connected
  R3 = Resistor [tolerance=±5% power=0.25 resistance=100k package=THT]  # not connected
  R4 = Resistor [tolerance=±5% power=0.25 resistance=100k package=THT]  # not connected

nets:
  5V: J1.pin1, J2.pin2, U1.output_voltage
  GND: J1.pin3, J1.pin10, J1.pin16, J2.pin1, J2.pin8, J2.pin16, X.GND, Y.GND, Z.GND, E.GND, X_en/step/dir/gnd.pin1, Y_en/step/dir/gnd.pin1, Z_en/step/dir/gnd.pin1, E_en/step/dir/gnd.pin1, X_endstop.pin3, Y_endstop.pin3, Z_endstop.pin3, E_endstop.pin3, J16.pin1, U1.GND, U2.GND
  3.3V: J1.pin4, J2.pin7, J2.pin15, X.VDD, Y.VDD, Z.VDD, E.VDD, X_endstop.pin1, Y_endstop.pin1, Z_endstop.pin1, E_endstop.pin1, U2.VCC, Temp1.pin1, Temp2.pin1
  N1: J1.pin7, X_endstop.pin2, Y_endstop.pin2, Z_endstop.pin2, E_endstop.pin2
  N2: J1.pin8, E.STEP, E_en/step/dir/gnd.pin3
  N3: J1.pin9, Q3.G
  N4: J1.pin11, X.DIR, X_en/step/dir/gnd.pin2
  N5: J1.pin12, X.STEP, X_en/step/dir/gnd.pin3
  N6: J1.pin13, X.ENABLE, Y.ENABLE, Z.ENABLE, E.ENABLE, X_en/step/dir/gnd.pin4, Y_en/step/dir/gnd.pin4, Z_en/step/dir/gnd.pin4, E_en/step/dir/gnd.pin4
  N7: J1.pin14, Temp2.pin2
  N8: J1.pin15, Temp1.pin2
  N9: J2.pin3, Y.DIR, Y_en/step/dir/gnd.pin2
  N10: J2.pin4, Q2.G
  N11: J2.pin5, E.DIR, E_en/step/dir/gnd.pin2
  N12: J2.pin6, Z.DIR, Z_en/step/dir/gnd.pin2
  N13: J2.pin9, Y.STEP, Y_en/step/dir/gnd.pin3
  N14: J2.pin10, U2.CS
  N15: J2.pin11, Q1.G
  N16: J2.pin12, U2.DO
  N17: J2.pin13, U2.DI
  N18: J2.pin14, U2.SCK
  N19: X.1B, X_motor.pin1
  N20: X.1A, X_motor.pin2
  N21: X.2A, X_motor.pin3
  N22: X.2B, X_motor.pin4
  12V: X.VMOT, Y.VMOT, Z.VMOT, E.VMOT, J16.pin2, U1.input_voltage
  N23: Y.1B, Y_motor.pin1
  N24: Y.1A, Y_motor.pin2
  N25: Y.2A, Y_motor.pin3
  N26: Y.2B, Y_motor.pin4
  N27: Z.STEP, Z_en/step/dir/gnd.pin3
  N28: Z.1B, Z_motor.pin1, Z2_motor.pin1
  N29: Z.1A, Z_motor.pin2, Z2_motor.pin2
  N30: Z.2A, Z_motor.pin3, Z2_motor.pin3
  N31: Z.2B, Z_motor.pin4, Z2_motor.pin4
  N32: E.1B, E_motor.pin1
  N33: E.1A, E_motor.pin2
  N34: E.2A, E_motor.pin3
  N35: E.2B, E_motor.pin4
