# Fritzing sketch esp32c3 (saved by Fritzing 0.9.10b)
circuit board: 9.81892cm x 9.36721cm
breadboards: 1

parts:
  J1 = female pin header, 16 pins [form="♀ (female)"]
  J2 = female pin header, 16 pins [form="♀ (female)"]
  Z = Pololu A4988 [package=SO16]
  J5 = female pin header, 4 pins [form="♀ (female)"]
  Z_motor = female pin header, 4 pins [form="♀ (female)"]
  J13 = female pin header, 3 pins [form="♀ (female)"]
  J16 = Screw terminal - 2 pins [package=THT]
  Q1 = MOSFET-NCHANNEL [package=to220v]
  Q2 = MOSFET-NCHANNEL [package=to220v]
  U1 = Voltage Regulator - 5V [package="TO220 [THT]"]
  U2 = microSD Socket [package=usd-socket-pp]
  J19 = female pin header, 2 pins [form="♀ (female)"]  # not connected
  J24 = female pin header, 2 pins [form="♀ (female)"]  # not connected
  J32 = female pin header, 2 pins [form="♀ (female)"]  # not connected
  Hotend = Screw terminal - 2 pins [package=THT]  # not connected
  Bed = Screw terminal - 2 pins [package=THT]  # not connected
  Z2_motor = female pin header, 4 pins [form="♀ (female)"]
  Temp1 = female pin header, 2 pins [form="♀ (female)"]
  Temp2 = female pin header, 2 pins [form="♀ (female)"]

nets:
  5V: J1.pin1, J2.pin2, U1.output_voltage
  GND: J1.pin3, J1.pin10, J1.pin16, J2.pin1, J2.pin8, J2.pin16, Z.GND, J5.pin1, J13.pin3, J16.pin1, U1.GND, U2.GND
  3.3V: J1.pin4, J2.pin7, J2.pin15, J13.pin1, U2.VCC, Temp1.pin1, Temp2.pin1
  N1: J1.pin7, J13.pin2
  N2: J1.pin14, Temp2.pin2
  N3: J1.pin15, Temp1.pin2
  N4: J2.pin4, Q2.G
  N5: J2.pin6, Z.DIR, J5.pin2
  N6: J2.pin10, U2.CS
  N7: J2.pin11, Q1.G
  N8: J2.pin12, U2.DO
  N9: J2.pin13, U2.DI
  N10: J2.pin14, U2.SCK
  N11: Z.ENABLE, J5.pin4
  N12: Z.STEP, J5.pin3
  N13: Z.1B, Z_motor.pin1, Z2_motor.pin1
  N14: Z.1A, Z_motor.pin2, Z2_motor.pin2
  N15: Z.2A, Z_motor.pin3, Z2_motor.pin3
  N16: Z.2B, Z_motor.pin4, Z2_motor.pin4
  N17: J16.pin2, U1.input_voltage
