# Fritzing sketch esp32c6 (saved by Fritzing 0.9.10b)
circuit board: 12.8222cm x 10.8326cm
breadboards: 1

parts:
  J1 = female pin header, 16 pins [form="♀ (female)"]
  J2 = female pin header, 16 pins [form="♀ (female)"]
  X = Pololu A4988 [package=SO16]
  Y = Pololu A4988 [package=SO16]
  Z = Pololu A4988 [package=SO16]
  E0_/_Z2 = Pololu A4988 [package=SO16]
  J3 = female pin header, 4 pins [form="♀ (female)"]
  J4 = female pin header, 4 pins [form="♀ (female)"]
  J5 = female pin header, 4 pins [form="♀ (female)"]
  J6 = female pin header, 4 pins [form="♀ (female)"]
  J7 = female pin header, 4 pins [form="♀ (female)"]
  J8 = female pin header, 4 pins [form="♀ (female)"]
  J9 = female pin header, 4 pins [form="♀ (female)"]
  J10 = female pin header, 4 pins [form="♀ (female)"]
  J11 = female pin header, 3 pins [form="♀ (female)"]  # not connected
  J12 = female pin header, 3 pins [form="♀ (female)"]  # not connected
  J13 = female pin header, 3 pins [form="♀ (female)"]  # not connected
  J14 = female pin header, 3 pins [form="♀ (female)"]  # not connected
  J15 = female pin header, 3 pins [form="♀ (female)"]  # not connected
  J16 = Screw terminal - 2 pins [package=THT]
  Q1 = MOSFET-NCHANNEL [package=to220v]  # not connected
  Q2 = MOSFET-NCHANNEL [package=to220v]  # not connected
  Q3 = MOSFET-NCHANNEL [package=to220v]  # not connected
  Q4 = MOSFET-NCHANNEL [package=to220v]  # not connected
  Part1 = Adafruit Ethernet FeatherWing [part_number="Adafruit #3201"]
  U1 = Voltage Regulator - 5V [package="TO220 [THT]"]
  E1 = Pololu A4988 [package=SO16]
  J17 = female pin header, 4 pins [form="♀ (female)"]
  J18 = female pin header, 4 pins [form="♀ (female)"]
  U2 = microSD Socket [package=usd-socket-pp]  # not connected
  J19 = female pin header, 2 pins [form="♀ (female)"]  # not connected
  J20 = female pin header, 2 pins [form="♀ (female)"]  # not connected
  J21 = female pin header, 2 pins [form="♀ (female)"]  # not connected
  J22 = female pin header, 2 pins [form="♀ (female)"]  # not connected
  J23 = female pin header, 2 pins [form="♀ (female)"]  # not connected
  J24 = female pin header, 2 pins [form="♀ (female)"]  # not connected
  J25 = female pin header, 2 pins [form="♀ (female)"]  # not connected
  J26 = female pin header, 2 pins [form="♀ (female)"]  # not connected
  J27 = female pin header, 2 pins [form="♀ (female)"]  # not connected
  J28 = female pin header, 2 pins [form="♀ (female)"]  # not connected
  J29 = female pin header, 2 pins [form="♀ (female)"]  # not connected
  J30 = female pin header, 2 pins [form="♀ (female)"]  # not connected
  J31 = female pin header, 2 pins [form="♀ (female)"]  # not connected
  J32 = female pin header, 2 pins [form="♀ (female)"]  # not connected
  J33 = female pin header, 2 pins [form="♀ (female)"]  # not connected
  J34 = female pin header, 3 pins [form="♀ (female)"]  # not connected
  J35 = female pin header, 3 pins [form="♀ (female)"]  # not connected
  J36 = Screw terminal - 2 pins [package=THT]  # not connected
  J37 = Screw terminal - 2 pins [package=THT]  # not connected
  J38 = Screw terminal - 2 pins [package=THT]  # not connected
  J39 = Screw terminal - 2 pins [package=THT]  # not connected

nets:
  N1: J1.pin1, U1.output_voltage
  GND: J1.pin3, J1.pin10, J1.pin16, J2.pin1, J2.pin8, J2.pin16, X.GND, Y.GND, Z.GND, E0_/_Z2.GND, J3.pin1, J4.pin1, J5.pin1, J6.pin1, J16.pin1, Part1.GND, U1.GND, E1.GND, J17.pin1
  N2: J1.pin4, J2.pin7, J2.pin15, Part1.3.3V
  N3: X.ENABLE, J3.pin4
  N4: X.STEP, J3.pin3
  N5: X.DIR, J3.pin2
  N6: X.1B, J7.pin1
  N7: X.1A, J7.pin2
  N8: X.2A, J7.pin3
  N9: X.2B, J7.pin4
  N10: Y.ENABLE, J4.pin4
  N11: Y.STEP, J4.pin3
  N12: Y.DIR, J4.pin2
  N13: Y.1B, J8.pin1
  N14: Y.1A, J8.pin2
  N15: Y.2A, J8.pin3
  N16: Y.2B, J8.pin4
  N17: Z.ENABLE, J5.pin4
  N18: Z.STEP, J5.pin3
  N19: Z.DIR, J5.pin2
  N20: Z.1B, J9.pin1
  N21: Z.1A, J9.pin2
  N22: Z.2A, J9.pin3
  N23: Z.2B, J9.pin4
  N24: E0_/_Z2.ENABLE, J6.pin4
  N25: E0_/_Z2.STEP, J6.pin3
  N26: E0_/_Z2.DIR, J6.pin2
  N27: E0_/_Z2.1B, J10.pin1
  N28: E0_/_Z2.1A, J10.pin2
  N29: E0_/_Z2.2A, J10.pin3
  N30: E0_/_Z2.2B, J10.pin4
  N31: J16.pin2, U1.input_voltage
  N32: E1.ENABLE, J17.pin4
  N33: E1.STEP, J17.pin3
  N34: E1.DIR, J17.pin2
  N35: E1.1B, J18.pin1
  N36: E1.1A, J18.pin2
  N37: E1.2A, J18.pin3
  N38: E1.2B, J18.pin4

custom parts:
  Adafruit Ethernet FeatherWing: Wireless is wonderful, but sometimes you want the strong reliability of a wire. If your Feather board is going to be part of a permanent installation, this Ethernet FeatherWing will let you add quick and easy wired Internet. Just plug in a standard ethernet cable, and run the Ethernet2 library for cross-platform networking. Ethernet is a tried-and-true networking standard. It's supported by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
